// Logisim project computer.circ as structural Verilog: 2 circuits, main circuit main
module main (
);
endmodule

module ALU (
  input  [7:0] in_1,
  input  [7:0] in_2,
  input  in_3,
  input  in_4,
  output out_5,
  output [7:0] out_6,
  output _0,
  output out_8
);

  wire [7:0] adder_1_out, subtractor_1_out;

  Adder adder_1 (.a(in_1), .b(in_2), .out(adder_1_out), .cout(out_5));  // open: cin
  Subtractor subtractor_1 (.a(in_1), .b(in_2), .out(subtractor_1_out), .bout(out_8));  // open: bin
  Multiplexer #(.width(8)) multiplexer_1 (
    .in0(adder_1_out), .in1(subtractor_1_out), .out(out_6), .sel(in_4));  // open: en
  nor nor_1 (_0, out_6[0], out_6[1], out_6[2], out_6[3], out_6[4], out_6[5], out_6[6], out_6[7]);

  // Other names for the same wires on the sheet: ADD = in_3; SUBTRACT = in_4

  // Notes on the sheet:
  //   Output
endmodule
